// Digital circuit 03-04.dig as structural Verilog
module _03_04 (
  input  [6:0] In
);

  wire xor_1_out, xor_2_out, xor_3_out, xor_4_out, xor_5_out, xor_6_out;

  xor xor_1 (xor_1_out, In[3], In[4]);
  xor xor_2 (xor_2_out, In[5], In[6]);
  xor xor_3 (xor_3_out, In[1], In[2]);
  xor xor_4 (xor_4_out, In[5], In[6]);
  xor xor_5 (xor_5_out, In[0], In[2]);
  xor xor_6 (xor_6_out, In[4], In[6]);
  // XOr xor_7 has open pins: In_1=xor_1_out, In_2=xor_2_out, out=open
  // XOr xor_8 has open pins: In_1=xor_3_out, In_2=xor_4_out, out=open
  // XOr xor_9 has open pins: In_1=xor_5_out, In_2=xor_6_out, out=open
endmodule
